# Fritzing sketch Home1 (saved by Fritzing 0.8.7b)
circuit board: 6.88566cm x 5.36311cm
breadboards: 2

parts:
  Arduino2 = Arduino Uno (Rev3)
  D1 = APA3010SF4C [package=apa3010sf4c]
  R1 = Resistor [tolerance=±5% resistance=56 package=THT]
  U1 = SN74HC08N [part_number=SN74HC08N package="DIP14 [THT]"]
  Q1 = NPN-Transistor [part_number=2N3904 package="TO92 [THT]"]
  D2 = APA3010SF4C [package=apa3010sf4c]
  Q2 = NPN-Transistor [part_number=2N3904 package="TO92 [THT]"]
  R2 = Resistor [tolerance=±5% resistance=56 package=THT]
  Q4A = NPN-Transistor [part_number=2N3904 package="TO92 [THT]"]
  Q4A_2 = NPN-Transistor [part_number=2N3904 package="TO92 [THT]"]
  R4A = Resistor [tolerance=±5% resistance=10 package=THT]
  R4 = Resistor [tolerance=±5% resistance=10k package=THT]
  D4 = APA3010SF4C [package=apa3010sf4c]
  R5 = Resistor [tolerance=±5% resistance=300 package=THT]
  R6 = Resistor [tolerance=±5% resistance=300 package=THT]
  R3 = Resistor [tolerance=±5% resistance=56 package=THT]
  D3 = APA3010SF4C [package=apa3010sf4c]
  Q3 = NPN-Transistor [part_number=2N3904 package="TO92 [THT]"]
  R7 = Resistor [tolerance=±5% resistance=300 package=THT]
  R8 = Resistor [tolerance=±5% resistance=300 package=THT]

nets (from the schematic view):
  N1: Arduino2.D8, U1.3A
  N2: Arduino2.D9_PWM, U1.2A
  N3: Arduino2.D10_PWM/SS, U1.1A
  N4: Arduino2.D11_PWM/MOSI, U1.1B, U1.2B, U1.3B, U1.4B
  N5: Arduino2.D7, U1.4A
  5V: Arduino2.5V, R1.Pin_0, U1.Vcc, R2.Pin_1, R4.Pin_0, D4.1, R3.Pin_1
  GND: Arduino2.GND, U1.GND, Q1.E, Q2.E, Q4A_2.E, R4A.Pin_1, Q3.E
  N6: D1.1, R1.Pin_1
  N7: D1.2, Q1.C
  N8: U1.1Y, R5.Pin_0
  N9: U1.2Y, R6.Pin_0
  N10: U1.3Y, R7.Pin_0
  N11: U1.4Y, R8.Pin_0
  N12: Q1.B, R5.Pin_1
  N13: D2.1, R2.Pin_0
  N14: D2.2, Q2.C
  N15: Q2.B, R6.Pin_1
  N16: Q4A.E, Q4A_2.B, R4A.Pin_0
  N17: Q4A.B, Q4A_2.C, R4.Pin_1, R8.Pin_1
  N18: Q4A.C, D4.2
  N19: R3.Pin_0, D3.1
  N20: D3.2, Q3.C
  N21: Q3.B, R7.Pin_1

notes:
  In this example, FSR values are read in through an 'Analog In' pin. The values are then used to control the blinking rate of an LED.
  Related examples: http://www.ladyada.net/learn/sensors/fsr.html
  http://itp.nyu.edu/physcomp/sensors/Reports/ForceSensorResistor
  Related code: http://arduino.cc/en/Tutorial/AnalogInput

custom parts:
  SN74HC08N: Quad 2-input positive-AND gates

// code stored in the sketch: AnalogInputFSR.ino
/*
  Analog Input
 Demonstrates analog input by reading an analog sensor on analog pin 0 and
 turning on and off a light emitting diode(LED)  connected to digital pin 13. 
 The amount of time the LED will be on and off depends on
 the value obtained by analogRead(). 
 
 The circuit:
 * Potentiometer attached to analog input 0
 * center pin of the potentiometer to the analog pin
 * one side pin (either one) to ground
 * the other side pin to +5V
 * LED anode (long leg) attached to digital output 13
 * LED cathode (short leg) attached to ground
 
 * Note: because most Arduinos have a built-in LED attached 
 to pin 13 on the board, the LED is optional.
 
 
 Created by David Cuartielles
 modified 30 Aug 2011
 By Tom Igoe
 
 This example code is in the public domain.
 
 http://arduino.cc/en/Tutorial/AnalogInput
 
 */

int sensorPin = 2;    // select the input pin for the potentiometer
int ledPin = 13;      // select the pin for the LED
int sensorValue = 0;  // variable to store the value coming from the sensor

void setup() {
  // declare the ledPin as an OUTPUT:
  pinMode(ledPin, OUTPUT);  
}

void loop() {
  // read the value from the sensor:
  sensorValue = analogRead(sensorPin);    
  // turn the ledPin on
  digitalWrite(ledPin, HIGH);  
  // stop the program for <sensorValue> milliseconds:
  delay(sensorValue);          
  // turn the ledPin off:        
  digitalWrite(ledPin, LOW);   
  // stop the program for for <sensorValue> milliseconds:
  delay(sensorValue);                  
}
